# Fritzing sketch pi-display-connections (saved by Fritzing 0.9.3b)

parts:
  MCU1 = Raspberry Pi Zero
  J1 = shrouded pin header, 16 pins [form="♂ (shrouded male)"]

nets:
  N1: MCU1.pin_1, J1.pin16
  N2: MCU1.pin_6, J1.pin1
  N3: MCU1.pin_18, J1.pin10
  N4: MCU1.pin_19, J1.pin3
  N5: MCU1.pin_22, J1.pin8
  N6: MCU1.pin_23, J1.pin15
  N7: MCU1.pin_24, J1.pin9

notes:
  OLED pins as viewed from back of PCB with connector on left
